// Digital circuit 74ls169.dig as structural Verilog
module _74ls169 (
  input  U_nD,
  input  CLK,
  input  A,
  input  B,
  input  C,
  input  D,
  input  nENP,
  input  GND,
  input  nLOAD,
  input  nENT,
  input  VCC,
  output Q_D,
  output Q_C,
  output Q_B,
  output Q_A,
  output nRCO
);

  wire _74193_1_pin4, _74193_1_pin5, and_3_out, nand_1_out, not_1_out;

  _74193 _74193_1 (
    .pin1(B), .pin2(Q_A), .pin3(Q_B), .pin4(_74193_1_pin4), .pin5(_74193_1_pin5), .pin6(Q_C), .pin7(Q_D),
    .pin8(GND), .pin9(D), .pin10(C), .pin11(nLOAD), .pin12(nRCO), .pin14(1'b0), .pin15(A), .pin16(VCC));  // open: pin13
  and and_1 (_74193_1_pin4, and_3_out, not_1_out);
  not not_1 (not_1_out, U_nD);
  and and_2 (_74193_1_pin5, U_nD, and_3_out);
  and and_3 (and_3_out, CLK, nand_1_out);
  nand nand_1 (nand_1_out, nENP, nENT);
endmodule
