// Digital circuit cpu-real.dig as structural Verilog
module cpu_real (
  input  Manual_clk,
  input  Clk_toggle,
  input  clock,
  output [7:0] out_4,
  output [7:0] out_5,
  output [7:0] out_6
);

  wire _7408_1_pin2, _7408_1_pin3, _7408_1_pin6, _7408_2_pin1, _7408_2_pin2, _7408_2_pin4, _7408_2_pin5,
       _7408_2_pin9, _7408_2_pin10, _74283_2_p1, _74377_2_pin3, _74377_2_pin4, AI, CLK, MAI;
  wire [1:0] _7486_1_pin3, _7486_1_pin11, _7486_2_pin3, _7486_2_pin11;
  wire [3:0] _74377_1_pin3, _74377_1_pin13;
  wire [7:0] b, flags;

  _74377 _74377_1 (
    .pin1(MAI), .pin2(out_4[0]), .pin3(_74377_1_pin3[0]), .pin4(_74377_1_pin3[1]), .pin5(out_4[1]),
    .pin6(out_4[2]), .pin7(_74377_1_pin3[2]), .pin8(_74377_1_pin3[3]), .pin9(out_4[3]), .pin10(1'b0),
    .pin11(CLK), .pin12(out_4[4]), .pin13(_74377_1_pin13[0]), .pin14(_74377_1_pin13[1]), .pin15(out_4[5]),
    .pin16(out_4[6]), .pin17(_74377_1_pin13[2]), .pin18(_74377_1_pin13[3]), .pin19(out_4[7]), .pin20(1'b1));
  _7408 _7408_1 (
    .pin1(Manual_clk), .pin2(_7408_1_pin2), .pin3(_7408_1_pin3), .pin4(Clk_toggle), .pin5(clock),
    .pin6(_7408_1_pin6), .pin7(1'b0), .pin9(1'b0), .pin10(1'b0), .pin12(1'b0), .pin13(1'b0), .pin14(1'b1));  // open: pin8, pin11
  _7432 _7432_1 (
    .pin1(1'b0), .pin2(1'b0), .pin4(1'b0), .pin5(1'b0), .pin7(1'b0), .pin8(CLK), .pin9(_7408_1_pin3),
    .pin10(_7408_1_pin6), .pin12(1'b0), .pin13(1'b0), .pin14(1'b1));  // open: pin3, pin6, pin11
  _7404 _7404_1 (
    .pin1(Clk_toggle), .pin2(_7408_1_pin2), .pin3(1'b0), .pin5(1'b0), .pin7(1'b0), .pin9(1'b0), .pin11(1'b0),
    .pin13(1'b0), .pin14(1'b1));  // open: pin4, pin6, pin8, pin10, pin12
  // _74245 _74245_1: pin names not known; wires that end beside it: 1'b1, 1'b1, 1'b1, 1'b0
  _74245 _74245_2 (
    .pin1(1'b1), .pin2(out_6[0]), .pin3(out_6[1]), .pin4(out_6[2]), .pin5(out_6[3]), .pin6(out_6[4]),
    .pin7(out_6[5]), .pin8(out_6[6]), .pin9(out_6[7]), .pin10(1'b0), .pin11(_74377_1_pin13[3]),
    .pin12(_74377_1_pin13[2]), .pin13(_74377_1_pin13[1]), .pin14(_74377_1_pin13[0]),
    .pin15(_74377_1_pin3[3]), .pin16(_74377_1_pin3[2]), .pin17(_74377_1_pin3[1]), .pin18(_74377_1_pin3[0]),
    .pin19(1'b1), .pin20(1'b1));
  _74377 _74377_2 (
    .pin1(1'b1), .pin2(flags[0]), .pin3(_74377_2_pin3), .pin4(_74377_2_pin4), .pin5(flags[1]),
    .pin6(flags[2]), .pin7(out_6[7]), .pin8(1'b0), .pin9(flags[3]), .pin10(1'b0), .pin11(CLK),
    .pin12(flags[4]), .pin13(1'b0), .pin14(1'b0), .pin15(flags[5]), .pin16(flags[6]), .pin17(1'b0),
    .pin18(1'b0), .pin19(flags[7]), .pin20(1'b1));
  _74377 _74377_3 (
    .pin1(1'b1), .pin2(b[0]), .pin3(_74377_1_pin3[0]), .pin4(_74377_1_pin3[1]), .pin5(b[1]), .pin6(b[2]),
    .pin7(_74377_1_pin3[2]), .pin8(_74377_1_pin3[3]), .pin9(b[3]), .pin10(1'b0), .pin11(CLK), .pin12(b[4]),
    .pin13(_74377_1_pin13[0]), .pin14(_74377_1_pin13[1]), .pin15(b[5]), .pin16(b[6]),
    .pin17(_74377_1_pin13[2]), .pin18(_74377_1_pin13[3]), .pin19(b[7]), .pin20(1'b1));
  _74377 _74377_4 (
    .pin1(AI), .pin2(out_5[0]), .pin3(_74377_1_pin3[0]), .pin4(_74377_1_pin3[1]), .pin5(out_5[1]),
    .pin6(out_5[2]), .pin7(_74377_1_pin3[2]), .pin8(_74377_1_pin3[3]), .pin9(out_5[3]), .pin10(1'b0),
    .pin11(CLK), .pin12(out_5[4]), .pin13(_74377_1_pin13[0]), .pin14(_74377_1_pin13[1]), .pin15(out_5[5]),
    .pin16(out_5[6]), .pin17(_74377_1_pin13[2]), .pin18(_74377_1_pin13[3]), .pin19(out_5[7]), .pin20(1'b1));
  // _74283 _74283_1: pin names not known; wires that end beside it: 1'b1
  _7408 _7408_2 (
    .pin1(_7408_2_pin1), .pin2(_7408_2_pin2), .pin3(_74377_2_pin4), .pin4(_7408_2_pin4), .pin5(_7408_2_pin5),
    .pin6(_7408_2_pin2), .pin7(1'b0), .pin8(_7408_2_pin1), .pin9(_7408_2_pin9), .pin10(_7408_2_pin10),
    .pin12(1'b0), .pin13(1'b0), .pin14(1'b1));  // open: pin11
  _7486 _7486_1 (
    .pin1(b[4]), .pin2(1'b0), .pin3(_7486_1_pin3[0]), .pin4(b[5]), .pin5(1'b0), .pin6(_7486_1_pin3[1]),
    .pin7(1'b0), .pin8(_7486_1_pin11[0]), .pin9(b[6]), .pin10(1'b0), .pin11(_7486_1_pin11[1]), .pin12(b[7]),
    .pin13(1'b0), .pin14(1'b1));
  // _74283 _74283_2: pin names not known; wires that end beside it: _74283_2_p1, _74377_2_pin3, 1'b0, 1'b1, 1'b0, _74283_2_p1, 1'b0
  _7402 _7402_1 (
    .pin1(_7408_2_pin5), .pin2(out_6[0]), .pin3(out_6[1]), .pin4(_7408_2_pin4), .pin5(out_6[2]),
    .pin6(out_6[3]), .pin7(1'b0), .pin8(out_6[4]), .pin9(out_6[5]), .pin10(_7408_2_pin10), .pin11(out_6[6]),
    .pin12(out_6[7]), .pin13(_7408_2_pin9), .pin14(1'b1));
  _7486 _7486_2 (
    .pin1(b[0]), .pin2(1'b0), .pin3(_7486_2_pin3[0]), .pin4(b[1]), .pin5(1'b0), .pin6(_7486_2_pin3[1]),
    .pin7(1'b0), .pin8(_7486_2_pin11[0]), .pin9(b[2]), .pin10(1'b0), .pin11(_7486_2_pin11[1]), .pin12(b[3]),
    .pin13(1'b0), .pin14(1'b1));
  // Pins of 1 and 8 bits meet at out_5
  // Pins of 1 and 8 bits meet at out_4
  // Pins of 1 and 8 bits meet at out_6

  // Other names for the same wires on the sheet: mar[7:0] = out_4; alu[7:0] = out_6; a[7:0] = out_5

  // Notes on the sheet:
  //   clock: Hz: 100
  //   Memory Address Register
  //   Clock
  //   A Register
  //   ALU
  //   Flags Register
  //   B Register
endmodule
