// Digital circuit cpu-realest.dig as structural Verilog
module cpu_realest (
  input  [7:0] MANUAL_ADDR,
  input  clock,
  input  in_3,
  input  in_4,
  output [7:0] out_5
);

  wire _28c256_1_p6, _28c256_1_p7, _28c256_1_p8, _28c256_1_p9, _28c256_1_p10, _28c256_1_p12, _28c256_1_p14,
       _28c256_1_p15, _28c256_1_p16, _28c256_2_p2, _28c256_2_p4, _28c256_2_p5, _28c256_2_p7, _28c256_2_p8,
       _28c256_2_p10, _28c256_2_p11, _28c256_2_p31, _28c256_2_p33, _28c256_2_p34, _28c256_2_p35,
       _7400_1_pin11, _7402_1_pin1, _7402_1_pin4, _7402_1_pin10, _7402_1_pin13, _7404_1_pin5, _7404_2_pin1,
       _7404_2_pin9, _7404_2_pin11, _7404_2_pin13, _7408_1_pin3, _7408_1_pin8, _7408_1_pin10, _7486_1_pin2,
       _7486_1_pin5, _7486_1_pin10, _7486_1_pin13, _74138_1_pin7, _74138_1_pin9, _74138_1_pin10,
       _74138_1_pin11, _74138_1_pin12, _74138_1_pin13, _74138_1_pin14, _74138_1_pin15, _74157_1_pin2,
       _74157_1_pin4, _74157_1_pin5, _74157_1_pin7, _74157_1_pin9, _74157_1_pin11, _74157_1_pin12,
       _74157_1_pin14, _74157_2_pin2, _74157_2_pin4, _74157_2_pin5, _74157_2_pin7, _74157_2_pin9,
       _74157_2_pin11, _74157_2_pin12, _74157_2_pin14, _74163_2_pin10, _74163_2_pin15, _74245_1_pin11,
       _74245_1_pin12, _74245_1_pin13, _74245_1_pin14, _74245_1_pin15, _74245_1_pin16, _74245_1_pin17,
       _74245_1_pin18, _74245_2_pin11, _74245_2_pin12, _74245_2_pin13, _74245_2_pin14, _74245_2_pin15,
       _74245_2_pin16, _74245_2_pin17, _74245_2_pin18, _74245_3_pin11, _74245_3_pin12, _74245_3_pin13,
       _74245_3_pin14, _74245_3_pin15, _74245_3_pin16, _74245_3_pin17, _74245_3_pin18, _74245_4_pin11,
       _74245_4_pin12, _74245_4_pin13, _74245_4_pin14, _74245_4_pin15, _74245_4_pin16, _74245_4_pin17,
       _74245_4_pin18, _74245_5_pin15, _74245_5_pin16, _74245_5_pin17, _74245_5_pin18, _74283_1_pin2,
       _74283_1_pin6, _74283_1_pin7, _74283_1_pin9, _74283_1_pin11, _74283_1_pin15, _74283_2_pin2,
       _74283_2_pin6, _74283_2_pin11, _74283_2_pin15, CE, CLK, dipswitch_1_out, HT, MANUAL_ADDR_out,
       multiplexer_1_out, nAI, nAO, nBI, nCO, nEO, nFI, nII, nJ, nMAI, nOI, nor_1_out, not_2_out, not_3_out,
       not_4_out, not_5_out, not_6_out, not_7_out, not_8_out, not_9_out, not_10_out, not_11_out, not_12_out,
       not_13_out, not_14_out, not_15_out, nRESET, nRI, nRO, nSPD, nSPE, nSPO, pulldown_1_out, SU, T0;
  wire [2:0] flags;
  wire [7:0] _74245_1_pin9;

  Multiplexer multiplexer_1 (.sel(in_4), .in_0(in_3), .in_1(clock), .out(multiplexer_1_out));
  not not_1 (nRESET, dipswitch_1_out);
  LED led_1 (.in(not_2_out));
  not not_2 (not_2_out, nSPD);
  LED led_2 (.in(not_3_out));
  not not_3 (not_3_out, nSPE);
  LED led_3 (.in(CE));
  LED led_4 (.in(not_4_out));
  not not_4 (not_4_out, nJ);
  LED led_5 (.in(not_5_out));
  not not_5 (not_5_out, nAI);
  LED led_6 (.in(not_6_out));
  not not_6 (not_6_out, nBI);
  LED led_7 (.in(SU));
  LED led_8 (.in(not_7_out));
  not not_7 (not_7_out, nMAI);
  LED led_9 (.in(nRI));
  LED led_10 (.in(not_8_out));
  not not_8 (not_8_out, nII);
  LED led_11 (.in(not_9_out));
  not not_9 (not_9_out, nOI);
  LED led_12 (.in(not_10_out));
  not not_10 (not_10_out, nFI);
  LED led_13 (.in(not_11_out));
  not not_11 (not_11_out, nSPO);
  LED led_14 (.in(T0));
  LED led_15 (.in(HT));
  LED led_16 (.in(not_12_out));
  not not_12 (not_12_out, nRO);
  LED led_17 (.in(not_13_out));
  not not_13 (not_13_out, nEO);
  LED led_18 (.in(not_14_out));
  not not_14 (not_14_out, nAO);
  LED led_19 (.in(not_15_out));
  not not_15 (not_15_out, nCO);
  LED led_20 (.in(CLK));
  and and_1 (CLK, multiplexer_1_out, ~HT);  // And
  DipSwitch dipswitch_1 (.out(dipswitch_1_out));
  _7400 _7400_1 (
    .pin1(1'b0), .pin2(1'b0), .pin4(1'b0), .pin5(1'b0), .pin7(1'b0), .pin9(1'b0), .pin10(1'b0),
    .pin11(_7400_1_pin11), .pin12(CLK), .pin13(nRI), .pin14(1'b1));  // open: pin3, pin6, pin8
  // _28c256 _28c256_1: pin names not known; wires that end beside it: 1'b1, 1'b0, 1'b1, flags[1], flags[2], _28c256_1_p6, _28c256_1_p7, _28c256_1_p8, _28c256_1_p9, _28c256_1_p10, flags[0], _28c256_1_p12, 1'b0, _28c256_1_p14, _28c256_1_p15, _28c256_1_p16
  _74ls169 _74ls169_1 ();
  PullDown pulldown_1 (.out(pulldown_1_out));
  nor nor_1 (nor_1_out, T0, ~nRESET);  // NOr
  _74163 _74163_1 (
    .pin1(nor_1_out), .pin2(CLK), .pin3(1'b0), .pin4(1'b0), .pin5(1'b0), .pin6(1'b0), .pin7(1'b1),
    .pin8(1'b0), .pin9(1'b1), .pin10(1'b1), .pin12(_28c256_1_p15), .pin13(_28c256_1_p9),
    .pin14(_28c256_1_p7), .pin16(1'b1));  // open: pin11, pin15
  // _28c256 _28c256_2: pin names not known; wires that end beside it: 1'b0, _28c256_2_p2, pulldown_1_out, _28c256_2_p4, _28c256_2_p5, SU, _28c256_2_p7, _28c256_2_p8, CE, _28c256_2_p10, _28c256_2_p11, 1'b0, 1'b1, 1'b0, 1'b1, flags[1], flags[2], _28c256_1_p6, _28c256_1_p7, _28c256_1_p8, _28c256_1_p9, _28c256_1_p10, flags[0], _28c256_1_p12, 1'b0, _28c256_1_p14, _28c256_1_p15, _28c256_1_p16, 1'b0, _28c256_2_p2, _28c256_2_p31, _28c256_2_p4, _28c256_2_p33, _28c256_2_p34, _28c256_2_p35, 1'b0
  DipSwitch u_MANUAL_ADDR (.out(MANUAL_ADDR_out));
  _74ls169 _74ls169_2 ();
  _74138 _74138_1 (
    .pin1(_28c256_1_p7), .pin2(_28c256_1_p9), .pin3(_28c256_1_p15), .pin4(1'b0), .pin5(1'b0), .pin6(1'b1),
    .pin7(_74138_1_pin7), .pin8(1'b0), .pin9(_74138_1_pin9), .pin10(_74138_1_pin10), .pin11(_74138_1_pin11),
    .pin12(_74138_1_pin12), .pin13(_74138_1_pin13), .pin14(_74138_1_pin14), .pin15(_74138_1_pin15),
    .pin16(1'b1));
  _74157 _74157_1 (
    .pin1(MANUAL_ADDR_out), .pin2(_74157_1_pin2), .pin3(MANUAL_ADDR[0]), .pin4(_74157_1_pin4),
    .pin5(_74157_1_pin5), .pin6(MANUAL_ADDR[1]), .pin7(_74157_1_pin7), .pin8(1'b0), .pin9(_74157_1_pin9),
    .pin10(MANUAL_ADDR[2]), .pin11(_74157_1_pin11), .pin12(_74157_1_pin12), .pin13(MANUAL_ADDR[3]),
    .pin14(_74157_1_pin14), .pin15(1'b0), .pin16(1'b1));
  _74245 _74245_1 (
    .pin1(1'b0), .pin2(_74245_1_pin9[0]), .pin3(_74245_1_pin9[1]), .pin4(_74245_1_pin9[2]),
    .pin5(_74245_1_pin9[3]), .pin6(_74245_1_pin9[4]), .pin7(_74245_1_pin9[5]), .pin8(_74245_1_pin9[6]),
    .pin9(_74245_1_pin9[7]), .pin10(1'b0), .pin11(_74245_1_pin11), .pin12(_74245_1_pin12),
    .pin13(_74245_1_pin13), .pin14(_74245_1_pin14), .pin15(_74245_1_pin15), .pin16(_74245_1_pin16),
    .pin17(_74245_1_pin17), .pin18(_74245_1_pin18), .pin19(nSPO), .pin20(1'b1));
  LED led_21 (.in(_74138_1_pin15));
  LED led_22 (.in(_74138_1_pin14));
  LED led_23 (.in(_74138_1_pin13));
  LED led_24 (.in(_74138_1_pin12));
  LED led_25 (.in(_74138_1_pin11));
  LED led_26 (.in(_74138_1_pin10));
  LED led_27 (.in(_74138_1_pin9));
  LED led_28 (.in(_74138_1_pin7));
  _7404 _7404_1 (
    .pin1(_28c256_2_p10), .pin2(nAI), .pin3(_28c256_2_p8), .pin4(nBI), .pin5(_7404_1_pin5), .pin6(nOI),
    .pin7(1'b0), .pin8(nSPD), .pin9(_28c256_2_p5), .pin10(nSPE), .pin11(_28c256_2_p7), .pin12(nJ),
    .pin13(_28c256_2_p11), .pin14(1'b1));
  _74157 _74157_2 (
    .pin1(MANUAL_ADDR_out), .pin2(_74157_2_pin2), .pin3(MANUAL_ADDR[4]), .pin4(_74157_2_pin4),
    .pin5(_74157_2_pin5), .pin6(MANUAL_ADDR[5]), .pin7(_74157_2_pin7), .pin8(1'b0), .pin9(_74157_2_pin9),
    .pin10(MANUAL_ADDR[6]), .pin11(_74157_2_pin11), .pin12(_74157_2_pin12), .pin13(MANUAL_ADDR[7]),
    .pin14(_74157_2_pin14), .pin15(1'b0), .pin16(1'b1));
  _7404 _7404_2 (
    .pin1(_7404_2_pin1), .pin2(nII), .pin3(_28c256_2_p31), .pin4(nMAI), .pin5(1'b0), .pin7(1'b0), .pin8(HT),
    .pin9(_7404_2_pin9), .pin10(T0), .pin11(_7404_2_pin11), .pin12(nFI), .pin13(_7404_2_pin13), .pin14(1'b1));  // open: pin6
  // _28c256 _28c256_3: pin names not known; wires that end beside it: 1'b1, 1'b0, _7400_1_pin11, 1'b0, 1'b0, _74157_2_pin12, 1'b0, _74157_2_pin9, 1'b0, _74157_2_pin7, 1'b0, _74157_2_pin4, nRO, _74157_1_pin12, 1'b0, _74157_1_pin9, 1'b0, _74157_1_pin7, _74245_1_pin9[7], _74157_1_pin4, _74245_1_pin9[0], _74245_1_pin9[1], _74245_1_pin9[2], 1'b0
  _74377 _74377_1 (
    .pin1(nMAI), .pin2(_74157_1_pin2), .pin3(_74245_1_pin9[0]), .pin4(_74245_1_pin9[1]),
    .pin5(_74157_1_pin5), .pin6(_74157_1_pin11), .pin7(_74245_1_pin9[2]), .pin8(_74245_1_pin9[3]),
    .pin9(_74157_1_pin14), .pin10(1'b0), .pin11(CLK), .pin12(_74157_2_pin2), .pin13(_74245_1_pin9[4]),
    .pin14(_74245_1_pin9[5]), .pin15(_74157_2_pin5), .pin16(_74157_2_pin11), .pin17(_74245_1_pin9[6]),
    .pin18(_74245_1_pin9[7]), .pin19(_74157_2_pin14), .pin20(1'b1));
  _74377 _74377_2 (
    .pin1(nII), .pin2(_28c256_2_p4), .pin3(_74245_1_pin9[0]), .pin4(_74245_1_pin9[1]), .pin5(_28c256_2_p2),
    .pin6(_28c256_1_p16), .pin7(_74245_1_pin9[2]), .pin8(_74245_1_pin9[3]), .pin9(_28c256_1_p14),
    .pin10(1'b0), .pin11(CLK), .pin12(_28c256_1_p12), .pin13(_74245_1_pin9[4]), .pin14(_74245_1_pin9[5]),
    .pin15(_28c256_1_p10), .pin16(_28c256_1_p8), .pin17(_74245_1_pin9[6]), .pin18(_74245_1_pin9[7]),
    .pin19(_28c256_1_p6), .pin20(1'b1));
  _74138 _74138_2 (
    .pin1(_28c256_2_p33), .pin2(_28c256_2_p34), .pin3(_28c256_2_p35), .pin4(1'b0), .pin5(1'b0), .pin6(1'b1),
    .pin7(nSPO), .pin8(1'b0), .pin9(_7404_2_pin11), .pin10(_7404_2_pin9), .pin11(nRO), .pin12(nEO),
    .pin13(nAO), .pin14(nCO), .pin16(1'b1));  // open: pin15
  PullDown pulldown_2 (.out(_74245_1_pin9[4]));
  PullDown pulldown_3 (.out(_74245_1_pin9[5]));
  PullDown pulldown_4 (.out(_74245_1_pin9[6]));
  PullDown pulldown_5 (.out(_74245_1_pin9[7]));
  PullDown pulldown_6 (.out(_74245_1_pin9[0]));
  PullDown pulldown_7 (.out(_74245_1_pin9[1]));
  PullDown pulldown_8 (.out(_74245_1_pin9[2]));
  PullDown pulldown_9 (.out(_74245_1_pin9[3]));
  _74245 _74245_2 (
    .pin1(1'b0), .pin2(_74245_1_pin9[0]), .pin3(_74245_1_pin9[1]), .pin4(_74245_1_pin9[2]),
    .pin5(_74245_1_pin9[3]), .pin6(_74245_1_pin9[4]), .pin7(_74245_1_pin9[5]), .pin8(_74245_1_pin9[6]),
    .pin9(_74245_1_pin9[7]), .pin10(1'b0), .pin11(_74245_2_pin11), .pin12(_74245_2_pin12),
    .pin13(_74245_2_pin13), .pin14(_74245_2_pin14), .pin15(_74245_2_pin15), .pin16(_74245_2_pin16),
    .pin17(_74245_2_pin17), .pin18(_74245_2_pin18), .pin19(nCO), .pin20(1'b1));
  _74245 _74245_3 (
    .pin1(1'b0), .pin2(_74245_1_pin9[0]), .pin3(_74245_1_pin9[1]), .pin4(_74245_1_pin9[2]),
    .pin5(_74245_1_pin9[3]), .pin6(_74245_1_pin9[4]), .pin7(_74245_1_pin9[5]), .pin8(_74245_1_pin9[6]),
    .pin9(_74245_1_pin9[7]), .pin10(1'b0), .pin11(_74245_3_pin11), .pin12(_74245_3_pin12),
    .pin13(_74245_3_pin13), .pin14(_74245_3_pin14), .pin15(_74245_3_pin15), .pin16(_74245_3_pin16),
    .pin17(_74245_3_pin17), .pin18(_74245_3_pin18), .pin19(nEO), .pin20(1'b1));
  _74245 _74245_4 (
    .pin1(1'b0), .pin2(_74245_1_pin9[0]), .pin3(_74245_1_pin9[1]), .pin4(_74245_1_pin9[2]),
    .pin5(_74245_1_pin9[3]), .pin6(_74245_1_pin9[4]), .pin7(_74245_1_pin9[5]), .pin8(_74245_1_pin9[6]),
    .pin9(_74245_1_pin9[7]), .pin10(1'b0), .pin11(_74245_4_pin11), .pin12(_74245_4_pin12),
    .pin13(_74245_4_pin13), .pin14(_74245_4_pin14), .pin15(_74245_4_pin15), .pin16(_74245_4_pin16),
    .pin17(_74245_4_pin17), .pin18(_74245_4_pin18), .pin19(nAO), .pin20(1'b1));
  Register #(.Bits(8)) register_1 (.D(_74245_1_pin9), .C(CLK), .en(~nOI), .Q(out_5));
  LED led_29 (.in(_74163_2_pin15));
  _74163 _74163_2 (
    .pin1(nRESET), .pin2(CLK), .pin3(_74245_1_pin9[4]), .pin4(_74245_1_pin9[5]), .pin5(_74245_1_pin9[6]),
    .pin6(_74245_1_pin9[7]), .pin7(CE), .pin8(1'b0), .pin9(nJ), .pin10(_74163_2_pin10),
    .pin11(_74245_2_pin11), .pin12(_74245_2_pin12), .pin13(_74245_2_pin13), .pin14(_74245_2_pin14),
    .pin15(_74163_2_pin15), .pin16(1'b1));
  _74283 _74283_1 (
    .pin1(_74245_3_pin13), .pin2(_74283_1_pin2), .pin3(_74245_4_pin13), .pin4(_74245_3_pin14),
    .pin5(_74245_4_pin14), .pin6(_74283_1_pin6), .pin7(_74283_1_pin7), .pin8(1'b0), .pin9(_74283_1_pin9),
    .pin10(_74245_3_pin11), .pin11(_74283_1_pin11), .pin12(_74245_4_pin11), .pin13(_74245_3_pin12),
    .pin14(_74245_4_pin12), .pin15(_74283_1_pin15), .pin16(1'b1));
  _74377 _74377_3 (
    .pin1(nAI), .pin2(_74245_4_pin18), .pin3(_74245_1_pin9[0]), .pin4(_74245_1_pin9[1]),
    .pin5(_74245_4_pin17), .pin6(_74245_4_pin16), .pin7(_74245_1_pin9[2]), .pin8(_74245_1_pin9[3]),
    .pin9(_74245_4_pin15), .pin10(1'b0), .pin11(CLK), .pin12(_74245_4_pin14), .pin13(_74245_1_pin9[4]),
    .pin14(_74245_1_pin9[5]), .pin15(_74245_4_pin13), .pin16(_74245_4_pin12), .pin17(_74245_1_pin9[6]),
    .pin18(_74245_1_pin9[7]), .pin19(_74245_4_pin11), .pin20(1'b1));
  _74163 _74163_3 (
    .pin1(nRESET), .pin2(CLK), .pin3(_74245_1_pin9[0]), .pin4(_74245_1_pin9[1]), .pin5(_74245_1_pin9[2]),
    .pin6(_74245_1_pin9[3]), .pin7(CE), .pin8(1'b0), .pin9(nJ), .pin10(1'b1), .pin11(_74245_2_pin15),
    .pin12(_74245_2_pin16), .pin13(_74245_2_pin17), .pin14(_74245_2_pin18), .pin15(_74163_2_pin10),
    .pin16(1'b1));
  _74283 _74283_2 (
    .pin1(_74245_3_pin17), .pin2(_74283_2_pin2), .pin3(_74245_4_pin17), .pin4(_74245_3_pin18),
    .pin5(_74245_4_pin18), .pin6(_74283_2_pin6), .pin7(SU), .pin8(1'b0), .pin9(_74283_1_pin7),
    .pin10(_74245_3_pin15), .pin11(_74283_2_pin11), .pin12(_74245_4_pin15), .pin13(_74245_3_pin16),
    .pin14(_74245_4_pin16), .pin15(_74283_2_pin15), .pin16(1'b1));
  _7402 _7402_1 (
    .pin1(_7402_1_pin1), .pin2(_74245_3_pin12), .pin3(_74245_3_pin11), .pin4(_7402_1_pin4),
    .pin5(_74245_3_pin16), .pin6(_74245_3_pin15), .pin7(1'b0), .pin8(_74245_3_pin13), .pin9(_74245_3_pin14),
    .pin10(_7402_1_pin10), .pin11(_74245_3_pin17), .pin12(_74245_3_pin18), .pin13(_7402_1_pin13), .pin14(1'b1));
  _7486 _7486_1 (
    .pin1(SU), .pin2(_7486_1_pin2), .pin3(_74283_1_pin6), .pin4(SU), .pin5(_7486_1_pin5),
    .pin6(_74283_1_pin2), .pin7(1'b0), .pin8(_74283_1_pin15), .pin9(SU), .pin10(_7486_1_pin10),
    .pin11(_74283_1_pin11), .pin12(SU), .pin13(_7486_1_pin13), .pin14(1'b1));
  _7408 _7408_1 (
    .pin1(_7402_1_pin4), .pin2(_7402_1_pin1), .pin3(_7408_1_pin3), .pin4(1'b0), .pin5(1'b0), .pin7(1'b0),
    .pin8(_7408_1_pin8), .pin9(_7408_1_pin3), .pin10(_7408_1_pin10), .pin11(_7408_1_pin10),
    .pin12(_7402_1_pin13), .pin13(_7402_1_pin10), .pin14(1'b1));  // open: pin6
  _74245 _74245_5 (
    .pin1(1'b0), .pin2(_74245_1_pin9[0]), .pin3(_74245_1_pin9[1]), .pin4(_74245_1_pin9[2]),
    .pin5(_74245_1_pin9[3]), .pin6(_74245_1_pin9[4]), .pin7(_74245_1_pin9[5]), .pin8(_74245_1_pin9[6]),
    .pin9(_74245_1_pin9[7]), .pin10(1'b0), .pin11(_7486_1_pin13), .pin12(_7486_1_pin10),
    .pin13(_7486_1_pin5), .pin14(_7486_1_pin2), .pin15(_74245_5_pin15), .pin16(_74245_5_pin16),
    .pin17(_74245_5_pin17), .pin18(_74245_5_pin18), .pin19(1'b1), .pin20(1'b1));
  _7486 _7486_2 (
    .pin1(SU), .pin2(_74245_5_pin18), .pin3(_74283_2_pin6), .pin4(SU), .pin5(_74245_5_pin17),
    .pin6(_74283_2_pin2), .pin7(1'b0), .pin8(_74283_2_pin15), .pin9(SU), .pin10(_74245_5_pin16),
    .pin11(_74283_2_pin11), .pin12(SU), .pin13(_74245_5_pin15), .pin14(1'b1));
  _74377 _74377_4 (
    .pin1(nBI), .pin2(_74245_5_pin18), .pin3(_74245_1_pin9[0]), .pin4(_74245_1_pin9[1]),
    .pin5(_74245_5_pin17), .pin6(_74245_5_pin16), .pin7(_74245_1_pin9[2]), .pin8(_74245_1_pin9[3]),
    .pin9(_74245_5_pin15), .pin10(1'b0), .pin11(CLK), .pin12(_7486_1_pin2), .pin13(_74245_1_pin9[4]),
    .pin14(_74245_1_pin9[5]), .pin15(_7486_1_pin5), .pin16(_7486_1_pin10), .pin17(_74245_1_pin9[6]),
    .pin18(_74245_1_pin9[7]), .pin19(_7486_1_pin13), .pin20(1'b1));
  _74377 _74377_5 (
    .pin1(nFI), .pin2(flags[0]), .pin3(_74283_1_pin9), .pin4(_7408_1_pin8), .pin5(flags[1]), .pin6(flags[2]),
    .pin7(_74245_3_pin11), .pin8(1'b0), .pin10(1'b0), .pin11(CLK), .pin13(1'b0), .pin14(1'b0), .pin17(1'b0),
    .pin18(1'b0), .pin20(1'b1));  // open: pin9, pin12, pin15, pin16, pin19

  // Notes on the sheet:
  //   clock: Hz: 100
  //   A REGISTER
  //   B REGISTER
endmodule
