// Digital circuit cpu.dig as structural Verilog
module cpu (
  input  clock,
  input  in_2,
  input  in_11,
  input  in_12,
  output [7:0] A_register,
  output [7:0] B_register,
  output [7:0] Mem_addr_register,
  output [7:0] Bus,
  output [7:0] ALU,
  output [7:0] Instruction_register,
  output [7:0] Output,
  output [7:0] Program_counter,
  output [7:0] Stack_pointer
);

  wire AI, and_1_out, and_3_out, AO, BI, CE, CLK, CO, counterpreset_1_ovf, EO, FI, HT, II, J, MAI,
       multiplexer_1_out, not_1_out, not_2_out, OI, or_1_out, RI, RO, SPD, SPE, SPO, Stack_Pointer_ovf, SU,
       T0;
  wire [2:0] add_1_c_o, flags, TCLK_out;
  wire [7:0] multiplexer_2_out, xor_1_out;
  wire [15:0] UCODE_d;

  LED led_1 (.in(SPD));
  LED led_2 (.in(SPE));
  LED led_3 (.in(CE));
  LED led_4 (.in(J));
  LED led_5 (.in(AI));
  LED led_6 (.in(BI));
  LED led_7 (.in(SU));
  LED led_8 (.in(MAI));
  LED led_9 (.in(RI));
  LED led_10 (.in(II));
  LED led_11 (.in(OI));
  LED led_12 (.in(FI));
  LED led_13 (.in(SPO));
  LED led_14 (.in(T0));
  LED led_15 (.in(HT));
  LED led_16 (.in(RO));
  LED led_17 (.in(EO));
  LED led_18 (.in(AO));
  LED led_19 (.in(CO));
  and and_1 (and_1_out, and_3_out, not_1_out);
  or or_1 (or_1_out, T0, in_2, and_1_out);
  Multiplexer multiplexer_1 (.sel(in_12), .in_0(in_11), .in_1(clock), .out(multiplexer_1_out));
  and and_2 (CLK, multiplexer_1_out, ~HT);  // And
  Register #(.Bits(8)) MAR (.D(Bus), .C(CLK), .en(MAI), .Q(Mem_addr_register));
  RAMSinglePort #(.AddrBits(8), .isProgramMemory("true"), .Bits(8)) ramsingleport_1 (
    .A(Mem_addr_register), .str(RI), .C(CLK), .ld(RO), .D(Bus));
  Register #(.Bits(8)) Out_reg (.D(Bus), .C(CLK), .en(OI), .Q(Output));
  Register #(.Bits(8)) Instr_reg (.D(Bus), .C(CLK), .en(II), .Q(Instruction_register));
  Register #(.Bits(8)) register_1 (.D(Bus), .C(CLK), .en(BI), .Q(B_register));
  not not_1 (not_1_out, TCLK_out[0]);
  not not_2 (not_2_out, CLK);
  and and_3 (and_3_out, TCLK_out[2], TCLK_out[1]);
  CounterPreset #(.Bits(3), .isProgramCounter("true")) TCLK (
    .en(1'b1), .C(not_2_out), .dir(1'b0), .in(3'b000), .ld(1'b0), .clr(or_1_out), .out(TCLK_out));  // open: ovf
  assign Bus = EO ? ALU : 8'bz;  // Driver driver_1
  assign Bus = SPO ? Stack_pointer : 8'bz;  // Driver driver_2
  assign Bus = CO ? Program_counter : 8'bz;  // Driver driver_3
  CounterPreset #(.Bits(8), .isProgramCounter("true")) counterpreset_1 (
    .en(CE), .C(CLK), .dir(1'b0), .in(Bus), .ld(J), .clr(in_2), .out(Program_counter),
    .ovf(counterpreset_1_ovf));
  assign Bus = AO ? A_register : 8'bz;  // Driver driver_4
  Register #(.Bits(8)) register_2 (.D(Bus), .C(CLK), .en(AI), .Q(A_register));
  Register #(.Bits(3)) Flags_reg (.D(add_1_c_o), .C(CLK), .en(FI), .Q(flags));
  LED led_20 (.in(Stack_Pointer_ovf));
  ROM #(.AddrBits(14), .Bits(16)) UCODE (
    .A({flags, TCLK_out, Instruction_register}), .sel(1'b1),
    .D({UCODE_d[15], SPD, SPE, CE, J, AI, BI, SU, MAI, RI, II, OI, FI, UCODE_d[2:0]}));
  LED led_21 (.in(counterpreset_1_ovf));
  Add #(.Bits(8)) add_1 (.a(A_register), .b(xor_1_out), .c_i(SU), .s(ALU), .c_o(add_1_c_o[0]));
  assign xor_1_out = B_register ^ multiplexer_2_out;  // XOr xor_1, 8 bits wide
  Multiplexer #(.Bits(8)) multiplexer_2 (.sel(SU), .in_0({8{1'b0}}), .in_1({8{1'b1}}), .out(multiplexer_2_out));
  CounterPreset #(.Bits(8)) u_Stack_Pointer (
    .en(SPE), .C(CLK), .dir(SPD), .in({8{1'b0}}), .ld(1'b0), .clr(in_2), .out(Stack_pointer),
    .ovf(Stack_Pointer_ovf));
  nor nor_1 (add_1_c_o[1], ALU[0], ALU[1], ALU[2], ALU[3], ALU[4], ALU[5], ALU[6], ALU[7]);
  BitSelector #(.Selector_Bits(3)) bitselector_1 (.in(ALU), .sel(3'b111), .out(add_1_c_o[2]));
  Decoder #(.Selector_Bits(3)) decoder_1 (
    .sel(UCODE_d[2:0]), .out_1(CO), .out_2(AO), .out_3(EO), .out_4(RO), .out_5(HT), .out_6(T0), .out_7(SPO));  // open: out_0

  // Other names for the same wires on the sheet: a[7:0] = A_register; b[7:0] = B_register;
  //   ir[7:0] = Instruction_register; mar[7:0] = Mem_addr_register; out[7:0] = Output; pc[7:0] = Program_counter;
  //   RESET = in_2; sp[7:0] = Stack_pointer

  // Notes on the sheet:
  //   clock: Hz: 100
  //   Clock
  //   Memory Address Register
  //   RAM
  //   Output Register
  //   Instruction Register
  //   B Register
  //   T-Clock
  //   Program Counter
  //   A Register
  //   ALU
  //   Flags Register
  //   Stack Pointer
  //   Control Logic
  //   UCODE loads ucode.hex
endmodule
